// Logisim project CST205_mod60_counter.circ as structural Verilog: 2 circuits, main circuit main
module main (
);

  wire and_1_out, and_2_out, and_3_out, clock_1_out;
  wire [2:0] n4_bit_asychronous_binary_counter_2_q0;
  wire [3:0] n4_bit_asychronous_binary_counter_1_q0;

  Clock clock_1 (.out(clock_1_out));
  and and_1 (and_1_out, n4_bit_asychronous_binary_counter_1_q0[1], n4_bit_asychronous_binary_counter_1_q0[3]);
  _4_bit_asychronous_binary_counter u_4_bit_asychronous_binary_counter_1 (
    .CLK(clock_1_out), .Q3(n4_bit_asychronous_binary_counter_1_q0[3]),
    .Q2(n4_bit_asychronous_binary_counter_1_q0[2]), .Q1(n4_bit_asychronous_binary_counter_1_q0[1]),
    .Q0(n4_bit_asychronous_binary_counter_1_q0[0]), .CLR(and_1_out));
  // Probe on n4_bit_asychronous_binary_counter_1_q0
  Hex_Digit_Display hex_digit_display_1 (.value({1'b0, n4_bit_asychronous_binary_counter_2_q0}));  // open: dp
  Hex_Digit_Display hex_digit_display_2 (.value(n4_bit_asychronous_binary_counter_1_q0));  // open: dp
  and and_2 (and_2_out, n4_bit_asychronous_binary_counter_2_q0[1], n4_bit_asychronous_binary_counter_2_q0[2]);
  and and_3 (and_3_out, n4_bit_asychronous_binary_counter_1_q0[0], n4_bit_asychronous_binary_counter_1_q0[3]);
  _4_bit_asychronous_binary_counter u_4_bit_asychronous_binary_counter_2 (
    .CLK(and_3_out), .Q2(n4_bit_asychronous_binary_counter_2_q0[2]),
    .Q1(n4_bit_asychronous_binary_counter_2_q0[1]), .Q0(n4_bit_asychronous_binary_counter_2_q0[0]),
    .CLR(and_2_out));  // open: Q3
  // Probe on {1'b0, n4_bit_asychronous_binary_counter_2_q0}
endmodule

module _4_bit_asychronous_binary_counter (
  input  CLK,
  input  CLR,
  output Q0,
  output Q1,
  output Q2,
  output Q3
);

  wire not_1_out, not_2_out, not_3_out, not_4_out;

  not not_1 (not_1_out, CLK);
  J_K_Flip_Flop j_k_ff_1 (.J(1'b1), .clk(not_1_out), .K(1'b1), .Q(Q0), .preset(1'b0), .reset(CLR));  // open: Qn, en
  not not_2 (not_2_out, Q0);
  J_K_Flip_Flop j_k_ff_2 (.J(1'b1), .clk(not_2_out), .K(1'b1), .Q(Q1), .preset(1'b0), .reset(CLR));  // open: Qn, en
  not not_3 (not_3_out, Q1);
  J_K_Flip_Flop j_k_ff_3 (.J(1'b1), .clk(not_3_out), .K(1'b1), .Q(Q2), .preset(1'b0), .reset(CLR));  // open: Qn, en
  not not_4 (not_4_out, Q2);
  J_K_Flip_Flop j_k_ff_4 (.J(1'b1), .clk(not_4_out), .K(1'b1), .Q(Q3), .preset(1'b0), .reset(CLR));  // open: Qn, en
endmodule
