// Logisim project CST205_mod60_sycounter.circ as structural Verilog: 3 circuits, main circuit main
module main (
);

  wire and_1_out, and_2_out, and_3_out, and_4_out, and_5_out, and_6_out, clock_1_out, clock_2_out;
  wire [2:0] n4_bit_asychronous_binary_counter_2_q0, n4_bit_sychronous_binary_counter_2_q0;
  wire [3:0] n4_bit_asychronous_binary_counter_1_q0, n4_bit_sychronous_binary_counter_1_q0;

  Clock clock_1 (.out(clock_1_out));
  and and_1 (and_1_out, n4_bit_asychronous_binary_counter_1_q0[1], n4_bit_asychronous_binary_counter_1_q0[3]);
  _4_bit_asychronous_binary_counter u_4_bit_asychronous_binary_counter_1 (
    .CLK(clock_1_out), .Q3(n4_bit_asychronous_binary_counter_1_q0[3]),
    .Q2(n4_bit_asychronous_binary_counter_1_q0[2]), .Q1(n4_bit_asychronous_binary_counter_1_q0[1]),
    .Q0(n4_bit_asychronous_binary_counter_1_q0[0]), .CLR(and_1_out));
  // Probe on n4_bit_asychronous_binary_counter_1_q0
  _4_bit_sychronous_binary_counter u_4_bit_sychronous_binary_counter_1 (
    .Q0(n4_bit_sychronous_binary_counter_1_q0[0]), .Q1(n4_bit_sychronous_binary_counter_1_q0[1]),
    .Q2(n4_bit_sychronous_binary_counter_1_q0[2]), .Q3(n4_bit_sychronous_binary_counter_1_q0[3]),
    .CLK(clock_2_out), .CLR(and_2_out));  // open: EN
  Hex_Digit_Display hex_digit_display_1 (.value({1'b0, n4_bit_asychronous_binary_counter_2_q0}));  // open: dp
  Clock clock_2 (.out(clock_2_out));
  Hex_Digit_Display hex_digit_display_2 (.value(n4_bit_asychronous_binary_counter_1_q0));  // open: dp
  Hex_Digit_Display hex_digit_display_3 (.value({1'b0, n4_bit_sychronous_binary_counter_2_q0}));  // open: dp
  and and_2 (and_2_out, n4_bit_sychronous_binary_counter_1_q0[1], n4_bit_sychronous_binary_counter_1_q0[3]);
  and and_3 (and_3_out, n4_bit_asychronous_binary_counter_2_q0[1], n4_bit_asychronous_binary_counter_2_q0[2]);
  and and_4 (and_4_out, n4_bit_asychronous_binary_counter_1_q0[0], n4_bit_asychronous_binary_counter_1_q0[3]);
  Hex_Digit_Display hex_digit_display_4 (.value(n4_bit_sychronous_binary_counter_1_q0));  // open: dp
  _4_bit_asychronous_binary_counter u_4_bit_asychronous_binary_counter_2 (
    .CLK(and_4_out), .Q2(n4_bit_asychronous_binary_counter_2_q0[2]),
    .Q1(n4_bit_asychronous_binary_counter_2_q0[1]), .Q0(n4_bit_asychronous_binary_counter_2_q0[0]),
    .CLR(and_3_out));  // open: Q3
  // Probe on {1'b0, n4_bit_asychronous_binary_counter_2_q0}
  _4_bit_sychronous_binary_counter u_4_bit_sychronous_binary_counter_2 (
    .Q0(n4_bit_sychronous_binary_counter_2_q0[0]), .Q1(n4_bit_sychronous_binary_counter_2_q0[1]),
    .Q2(n4_bit_sychronous_binary_counter_2_q0[2]), .EN(and_5_out), .CLK(clock_2_out), .CLR(and_6_out));  // open: Q3
  and and_5 (and_5_out, n4_bit_sychronous_binary_counter_1_q0[3], n4_bit_sychronous_binary_counter_1_q0[0]);
  and and_6 (and_6_out, n4_bit_sychronous_binary_counter_2_q0[2], n4_bit_sychronous_binary_counter_2_q0[1]);
endmodule

module _4_bit_asychronous_binary_counter (
  input  CLK,
  input  CLR,
  output Q0,
  output Q1,
  output Q2,
  output Q3
);

  wire not_1_out, not_2_out, not_3_out, not_4_out;

  not not_1 (not_1_out, CLK);
  J_K_Flip_Flop j_k_ff_1 (.J(1'b1), .clk(not_1_out), .K(1'b1), .Q(Q0), .preset(1'b0), .reset(CLR));  // open: Qn, en
  not not_2 (not_2_out, Q0);
  J_K_Flip_Flop j_k_ff_2 (.J(1'b1), .clk(not_2_out), .K(1'b1), .Q(Q1), .preset(1'b0), .reset(CLR));  // open: Qn, en
  not not_3 (not_3_out, Q1);
  J_K_Flip_Flop j_k_ff_3 (.J(1'b1), .clk(not_3_out), .K(1'b1), .Q(Q2), .preset(1'b0), .reset(CLR));  // open: Qn, en
  not not_4 (not_4_out, Q2);
  J_K_Flip_Flop j_k_ff_4 (.J(1'b1), .clk(not_4_out), .K(1'b1), .Q(Q3), .preset(1'b0), .reset(CLR));  // open: Qn, en
endmodule

module _4_bit_sychronous_binary_counter (
  input  CLR,
  input  EN,
  input  CLK,
  output Q0,
  output Q1,
  output Q2,
  output Q3
);

  wire and_1_out, and_2_out;

  T_Flip_Flop t_ff_1 (.clk(CLK), .T(1'b1), .Q(Q0), .reset(CLR), .en(EN));  // open: Qn, preset
  T_Flip_Flop t_ff_2 (.clk(CLK), .T(Q0), .Q(Q1), .reset(CLR), .en(EN));  // open: Qn, preset
  and and_1 (and_1_out, Q1, Q0);
  T_Flip_Flop t_ff_3 (.clk(CLK), .T(and_1_out), .Q(Q2), .reset(CLR), .en(EN));  // open: Qn, preset
  and and_2 (and_2_out, Q2, and_1_out);
  T_Flip_Flop t_ff_4 (.clk(CLK), .T(and_2_out), .Q(Q3), .reset(CLR), .en(EN));  // open: Qn, preset
endmodule
