// Logisim project compare.circ as structural Verilog: 4 circuits, main circuit main
module main (
  input  [2:0] in_1,
  input  [2:0] in_2,
  output out_3,
  output out_4,
  output out_5
);

  X_Y x_y_1 (.in_1(in_1), .in_2(in_2), .XY(out_3));
  X_Y_2 x_y_2 (.in_1(in_1), .in_2(in_2), .XY2(out_4));
  X_Y_2_2 x_y_3 (.XY2(out_5), .in_1(in_1), .in_2(in_2));
endmodule

module X_Y (
  input  [2:0] in_1,
  input  [2:0] in_2,
  output XY
);

  wire and_1_out, and_2_out, not_1_out, not_2_out, not_3_out, not_4_out, not_5_out, not_6_out;

  not not_1 (not_1_out, in_1[0]);
  not not_2 (not_2_out, in_1[1]);
  not not_3 (not_3_out, in_1[2]);
  not not_4 (not_4_out, in_2[0]);
  not not_5 (not_5_out, in_2[1]);
  not not_6 (not_6_out, in_2[2]);
  and and_1 (and_1_out, not_1_out, not_2_out, not_3_out, not_4_out, not_5_out, not_6_out);
  and and_2 (and_2_out, in_1[0], in_1[1], in_1[2], in_2[0], in_2[1], in_2[2]);
  or or_1 (XY, and_1_out, and_2_out);
endmodule

module X_Y_2 (
  input  [2:0] in_1,
  input  [2:0] in_2,
  output XY2
);

  wire and_1_out, and_2_out, and_3_out, not_1_out, not_2_out, not_3_out;

  not not_1 (not_1_out, in_2[2]);
  not not_2 (not_2_out, in_2[1]);
  not not_3 (not_3_out, in_2[0]);
  and and_1 (and_1_out, in_1[2], not_1_out);
  and and_2 (and_2_out, in_1[2], in_2[2], in_1[1], not_2_out);
  and and_3 (and_3_out, in_1[2], in_2[2], in_1[1], in_2[1], in_1[0], not_3_out);
  or or_1 (XY2, and_1_out, and_2_out, and_3_out);
endmodule

module X_Y_2_2 (
  input  [2:0] in_1,
  input  [2:0] in_2,
  output XY2
);

  wire and_1_out, and_2_out, and_3_out, not_1_out, not_2_out, not_3_out;

  not not_1 (not_1_out, in_2[2]);
  not not_2 (not_2_out, in_2[1]);
  not not_3 (not_3_out, in_2[0]);
  and and_1 (and_1_out, in_1[2], not_1_out);
  and and_2 (and_2_out, in_1[2], in_2[2], in_1[1], not_2_out);
  and and_3 (and_3_out, in_1[2], in_2[2], in_1[1], in_2[1], in_1[0], not_3_out);
  or or_1 (XY2, and_1_out, and_2_out, and_3_out);
endmodule
