// Logisim project shift.circ as structural Verilog
module main (
  output [3:0] out_1,
  output out_2,
  output [3:0] out_3,
  output out_4
);

  wire clock_1_out;

  Clock clock_1 (.out(clock_1_out));
  right_shift_register right_shift_register_1 (
    .Input(1'b1), .CLK(clock_1_out), .out_3(out_1[3]), .out_4(out_1[2]), .out_5(out_1[1]), .out_6(out_1[0]),
    .Output(out_2));
  left_shift_register left_shift_register_1 (
    .Input(1'b1), .CLK(clock_1_out), .Output(out_4), .out_4(out_3[0]), .out_5(out_3[1]), .out_6(out_3[2]),
    .out_7(out_3[3]));
endmodule

module right_shift_register (
  input  Input,
  input  CLK,
  output out_3,
  output out_4,
  output out_5,
  output out_6,
  output Output
);

  D_Flip_Flop d_ff_1 (.clk(CLK), .D(Input), .Q(out_3));  // open: Qn, preset, en, reset
  D_Flip_Flop d_ff_2 (.clk(CLK), .D(out_3), .Q(out_4));  // open: Qn, preset, en, reset
  D_Flip_Flop d_ff_3 (.clk(CLK), .D(out_4), .Q(out_5));  // open: Qn, preset, en, reset
  D_Flip_Flop d_ff_4 (.clk(CLK), .D(out_5), .Q(out_6));  // open: Qn, preset, en, reset

  assign Output = out_6;
endmodule

module left_shift_register (
  input  Input,
  input  CLK,
  output Output,
  output out_4,
  output out_5,
  output out_6,
  output out_7
);

  D_Flip_Flop d_ff_1 (.clk(CLK), .D(Input), .Q(out_4));  // open: Qn, preset, en, reset
  D_Flip_Flop d_ff_2 (.clk(CLK), .D(out_4), .Q(out_5));  // open: Qn, preset, en, reset
  D_Flip_Flop d_ff_3 (.clk(CLK), .D(out_5), .Q(out_6));  // open: Qn, preset, en, reset
  D_Flip_Flop d_ff_4 (.clk(CLK), .D(out_6), .Q(out_7));  // open: Qn, preset, en, reset

  assign Output = out_4;
endmodule
